# Fritzing sketch Core Module (saved by Fritzing 0.9.3b)
perfboards: 1

parts:
  Teensy_3_1 = Teensy 3.1
  J1 = female pin header, 2 pins [form="♀ (female)"]
  J2 = female pin header, 4 pins [form="♀ (female)"]
  J3 = female pin header, 9 pins [form="♀ (female)"]
  R1 = Resistor [tolerance=±5% resistance=100 package=THT]
  J4 = female pin header, 3 pins [form="♀ (female)"]
  J5 = female pin header, 3 pins [form="♀ (female)"]
  J6 = female pin header, 2 pins [form="♀ (female)"]
  R2 = Resistor [tolerance=±5% resistance=4.7k package=THT]

nets:
  N1: Teensy_3_1.GND, J2.pin4
  N2: Teensy_3_1.D0, J2.pin3
  N3: Teensy_3_1.D1, J2.pin2
  N4: Teensy_3_1.D2, J2.pin1
  N5: Teensy_3_1.D9, J3.pin5
  N6: Teensy_3_1.D10, J3.pin7
  N7: Teensy_3_1.D11, J3.pin4
  N8: Teensy_3_1.D12, J3.pin1
  N9: Teensy_3_1.D13, J3.pin3
  N10: Teensy_3_1.A0/D14, J3.pin6
  N11: Teensy_3_1.A1/D15, J4.pin2
  N12: Teensy_3_1.A2/D16, J5.pin2
  N13: Teensy_3_1.A3/D17, J6.pin1, R2.Pin_0
  N14: Teensy_3_1.AGND, J1.pin1
  N15: Teensy_3_1.Vin, J1.pin2
  N16: J3.pin2, R1.Pin_1

notes:
  SDO (MISO)
  LED
  SCK
  SDI (MOSI)
  RESET
  CS
  GND
  VCC
  DC
