# Fritzing sketch LED Controller (saved by Fritzing 0.9.3b)
perfboards: 1

parts:
  Q1 = Basic FET N-Channel [package="TO220 [THT]"]  # not connected
  Q2 = Basic FET N-Channel [package="TO220 [THT]"]  # not connected
  Q3 = Basic FET N-Channel [package="TO220 [THT]"]  # not connected
  H1 = polarizedheader 4pin 0.156in [package=THT]
  H2 = polarizedheader 4pin 0.156in [package=THT]
  R1 = Resistor [tolerance=±5% resistance=220 package="0402 [SMD]"]  # not connected
  R2 = Resistor [tolerance=±5% resistance=220 package="0402 [SMD]"]  # not connected
  R3 = Resistor [tolerance=±5% resistance=220 package="0402 [SMD]"]  # not connected
  J1 = female pin header, 2 pins [form="♀ (female)"]

nets:
  N1: H1.pin4, J1.pin1
  N2: H2.pin1, J1.pin2
