# Fritzing sketch Wiring Layout v2 (saved by Fritzing 0.9.3b)
perfboards: 4

parts:
  J4 = Power Jack [package=power_jack_smd]
  Swtich_Connection = Header 3 [package=molex-1x3_lock]
  J5 = Power Jack [package=power_jack_smd]
  C3 = Electrolytic Capacitor [capacitance=999µF package="100 mil [THT, electrolytic]"]
  Teensy1 = Teensy 3.0
  R1 = Resistor [tolerance=±5% resistance=500 package=THT]
  Touch_Poteniometer = polarizedheader 4pin 0.156in [package=THT]
  LED_60 = Header 3 [package=molex-1x3_lock]
  LED_144 = Header 3 [package=molex-1x3_lock]
  C6 = Electrolytic Capacitor [capacitance=999µF package="100 mil [THT, electrolytic]"]
  R3 = Resistor [tolerance=±5% resistance=500 package=THT]
  LED_144_2 = Header 3 [package=molex-1x3_lock]
  C7 = Electrolytic Capacitor [capacitance=999µF package="100 mil [THT, electrolytic]"]

nets:
  N1: J4.GND, LED_144.2, C6.+, LED_144_2.1, C7.+
  N2: J4.GNDBREAK, Teensy1.GND, LED_144.1, LED_144.3, C6.-, C7.-
  N3: Swtich_Connection.1, Teensy1.A6/D20
  N4: Swtich_Connection.2, J5.GNDBREAK, C3.+, Teensy1.Vin, Touch_Poteniometer.pin3, LED_60.2
  N5: Swtich_Connection.3, J5.GND, C3.-, Teensy1.AGND, Touch_Poteniometer.pin4, LED_60.1
  N6: Teensy1.A4/D18, Touch_Poteniometer.pin2
  N7: Teensy1.A5/D19, Touch_Poteniometer.pin1
  N8: Teensy1.A8/D22, R3.Pin_1
  N9: Teensy1.A9/D23, R1.Pin_1
  N10: R1.Pin_0, LED_60.3
  N11: R3.Pin_0, LED_144_2.2
