# Fritzing sketch Wiring Layout v3 (saved by Fritzing 0.9.3b)
perfboards: 3

parts:
  J4 = Power Jack [package=power_jack_smd]
  Swtich_Connection = Header 3 [package=molex-1x3_lock]
  C3 = Electrolytic Capacitor [capacitance=999µF package="100 mil [THT, electrolytic]"]
  Teensy1 = Teensy 3.0
  R1 = Resistor [tolerance=±5% resistance=500 package=THT]
  Touch_Poteniometer = polarizedheader 4pin 0.156in [package=THT]
  LED_60 = Header 3 [package=molex-1x3_lock]
  LED_144 = Header 3 [package=molex-1x3_lock]
  C6 = Electrolytic Capacitor [capacitance=999µF package="100 mil [THT, electrolytic]"]
  R3 = Resistor [tolerance=±5% resistance=500 package=THT]
  LED_144_2 = Header 3 [package=molex-1x3_lock]
  C7 = Electrolytic Capacitor [capacitance=999µF package="100 mil [THT, electrolytic]"]
  TRS1 = Audio Jack (TRS) 3.5mm [package="PG203J [THT]"]
  Audio_Shield = polarizedheader 4pin 0.156in [package=THT]

nets:
  GND: J4.GND, Swtich_Connection.3, C3.+, Teensy1.Vin, Touch_Poteniometer.pin3, LED_60.2, LED_144.2, C6.+, LED_144_2.1, C7.+
  N1: J4.GNDBREAK, Swtich_Connection.2, C3.-, Teensy1.GND, Teensy1.AGND, Touch_Poteniometer.pin4, LED_60.1, LED_144.1, LED_144.3, C6.-, C7.-, TRS1.Sleeve, Audio_Shield.pin2, Audio_Shield.pin3
  N2: Swtich_Connection.1, Teensy1.A6/D20
  N3: Teensy1.A4/D18, Touch_Poteniometer.pin2
  N4: Teensy1.A5/D19, Touch_Poteniometer.pin1
  N5: Teensy1.A8/D22, R3.Pin_1
  N6: Teensy1.A9/D23, R1.Pin_1
  N7: R1.Pin_0, LED_60.3
  N8: R3.Pin_0, LED_144_2.2
  N9: TRS1.Ring, Audio_Shield.pin1
  N10: TRS1.Tip, Audio_Shield.pin4
