# Fritzing sketch Wiring Layout v4 (saved by Fritzing 0.9.3b)
perfboards: 3
stripboards: 3

parts:
  J4 = Power Jack [package=power_jack_smd]
  Teensy1 = Teensy 3.0
  Touch_Pot = polarizedheader 4pin 0.156in [package=THT]
  Audio_Shield = polarizedheader 4pin 0.156in [package=THT]
  Switch = Header 3 [package=molex-1x3_lock]
  JP1 = Header 2 [package=molex-1x2_lock]
  JP2 = Header 2 [package=molex-1x2_lock]  # not connected
  JP3 = Header 2 [package=molex-1x2_lock]
  part = Header 3 [package=molex-1x3_lock]  # not connected
  C8 = Electrolytic Capacitor [capacitance=999µF package="100 mil [THT, electrolytic]"]  # not connected
  R4 = Resistor [tolerance=±5% resistance=470 package=THT]
  C9 = Electrolytic Capacitor [capacitance=999µF package="100 mil [THT, electrolytic]"]  # not connected
  JP5 = Header 3 [package=molex-1x3_lock]  # not connected
  JP7 = Header 3 [package=molex-1x3_lock]
  C10 = Electrolytic Capacitor [capacitance=999µF package="100 mil [THT, electrolytic]"]  # not connected
  JP8 = Header 2 [package=molex-1x2_lock]
  TRS1 = Audio Jack (TRS) 3.5mm [package="PG203J [THT]"]
  Audio_In = polarizedheader 4pin 0.156in [package=THT]
  JP9 = Header 2 [package=molex-1x2_lock]
  JP10 = Header 2 [package=molex-1x2_lock]
  LED3 = LED - 3mm [color="Red (633nm)" package="3 mm [THT]"]
  R5 = Resistor [tolerance=±5% resistance=220 package=THT]

nets:
  N1: J4.GND, JP1.1
  GND: Teensy1.GND, Teensy1.AGND, Teensy1.Vin, Touch_Pot.pin3, Touch_Pot.pin4, Switch.2, Switch.3, JP3.2, JP8.2, JP9.1, JP9.2, JP10.2, LED3.anode, R5.Pin_0
  N2: Teensy1.D1, JP8.1, JP10.1
  N3: Teensy1.D2, R5.Pin_1
  N4: Teensy1.A4/D18, Touch_Pot.pin2
  N5: Teensy1.A5/D19, Touch_Pot.pin1
  N6: Teensy1.A8/D22, Switch.1, LED3.cathode
  N7: Audio_Shield.pin1, TRS1.Ring, Audio_In.pin1
  N8: Audio_Shield.pin2, Audio_Shield.pin3, Audio_In.pin2, Audio_In.pin3
  N9: Audio_Shield.pin4, TRS1.Tip, Audio_In.pin4
  N10: R4.Pin_1, JP7.3
