# Fritzing sketch Wiring Layout (saved by Fritzing 0.9.3b)
perfboards: 1

parts:
  J4 = Power Jack [package=power_jack_smd]
  Touch_Potentiometer = POT [package=alps_pot]  # not connected
  LED_Switch = Toggle Switch [package=THT]  # not connected
  LED_Output_I = Header 3 [package=molex-1x3_lock]
  U2 = AUDIO-JACK2 [package=audio-jack-3.5mm-smd]  # not connected
  Pot_Connection = Header 3 [package=molex-1x3_lock]
  Swtich_Connection = Header 3 [package=molex-1x3_lock]
  J5 = Power Jack [package=power_jack_smd]
  LED_Output_II = Header 3 [package=molex-1x3_lock]
  LED_Output_II_2 = Header 3 [package=molex-1x3_lock]
  C3 = Electrolytic Capacitor [capacitance=999µF package="100 mil [THT, electrolytic]"]
  R2 = Resistor [tolerance=±5% resistance=500 package=THT]
  C4 = Electrolytic Capacitor [capacitance=999µF package="100 mil [THT, electrolytic]"]
  C5 = Electrolytic Capacitor [capacitance=999µF package="100 mil [THT, electrolytic]"]  # not connected
  Teensy1 = Teensy 3.0
  R1 = Resistor [tolerance=±5% resistance=500 package=THT]

nets:
  GND: J4.GND, LED_Output_I.1, Swtich_Connection.3, C3.+, Teensy1.Vin
  N1: J4.GNDBREAK, LED_Output_I.2, Swtich_Connection.2, Teensy1.AGND
  N2: LED_Output_I.3, R1.Pin_1
  N3: Pot_Connection.1, Teensy1.A9/D23
  N4: Pot_Connection.2, J5.GNDBREAK, LED_Output_II.3
  N5: Swtich_Connection.1, Teensy1.A8/D22
  N6: J5.GND, LED_Output_II.1, C4.+
  N7: LED_Output_II_2.3, R2.Pin_1
  N8: R2.Pin_0, Teensy1.D1
  N9: Teensy1.D2, R1.Pin_0
